// Logisim project m1_36863.circ as structural Verilog: 12 circuits, main circuit TESTBENCH
module NOR_T (
  input  X,
  input  Y,
  output Z
);

  wire transistor_1_out;

  Transistor transistor_1 (.in(1'b1), .out(transistor_1_out), .gate(X));
  Transistor transistor_2 (.in(transistor_1_out), .out(Z), .gate(Y));
  Transistor #(.\type ("n")) transistor_3 (.in(1'b0), .out(Z), .gate(X));
  Transistor #(.\type ("n")) transistor_4 (.in(1'b0), .out(Z), .gate(Y));

  // Notes on the sheet:
  //   NOR_T: Z = (X + Y)'  -- transistors only
  //   pull-up: 2 P-type in series
  //   pull-down: 2 N-type in parallel
endmodule

module NOT_NOR (
  input  X,
  output Y
);

  NOR_T nor_t_1 (.X(X), .Y(X), .Z(Y));

  // Notes on the sheet:
  //   NOT_NOR: Y = X' = (X + X)'
endmodule

module OR_NOR (
  input  X,
  input  Y,
  output Z
);

  wire nor_t_1_z;

  NOR_T nor_t_1 (.X(X), .Y(Y), .Z(nor_t_1_z));
  NOT_NOR not_nor_1 (.X(nor_t_1_z), .Y(Z));

  // Notes on the sheet:
  //   OR_NOR: Z = X + Y = ((X + Y)')'
endmodule

module AND_NOR (
  input  X,
  input  Y,
  output Z
);

  wire not_nor_1_y, not_nor_2_y;

  NOT_NOR not_nor_1 (.X(X), .Y(not_nor_1_y));
  NOR_T nor_t_1 (.X(not_nor_1_y), .Y(not_nor_2_y), .Z(Z));
  NOT_NOR not_nor_2 (.X(Y), .Y(not_nor_2_y));

  // Notes on the sheet:
  //   AND_NOR: Z = XY = (X' + Y')'
endmodule

module XOR_SOP (
  input  X,
  input  Y,
  output Z
);

  wire and_nor_1_z, and_nor_2_z, not_nor_1_y, not_nor_2_y;

  NOT_NOR not_nor_1 (.X(X), .Y(not_nor_1_y));
  AND_NOR and_nor_1 (.X(not_nor_1_y), .Y(Y), .Z(and_nor_1_z));
  OR_NOR or_nor_1 (.X(and_nor_1_z), .Y(and_nor_2_z), .Z(Z));
  NOT_NOR not_nor_2 (.X(Y), .Y(not_nor_2_y));
  AND_NOR and_nor_2 (.X(X), .Y(not_nor_2_y), .Z(and_nor_2_z));

  // Notes on the sheet:
  //   XOR_SOP: Z = X'Y + XY'
endmodule

module MAJ3 (
  input  X,
  input  Y,
  input  Z,
  output OUT
);

  wire and_1_out, and_2_out, and_3_out, and_4_out;

  and and_1 (and_1_out, ~X, Y, Z);  // AND_Gate
  and and_2 (and_2_out, X, ~Y, Z);  // AND_Gate
  and and_3 (and_3_out, X, Y, ~Z);  // AND_Gate
  and and_4 (and_4_out, X, Y, Z);
  or or_1 (OUT, and_1_out, and_2_out, and_3_out, and_4_out);

  // Notes on the sheet:
  //   MAJ3: OUT = X'YZ + XY'Z + XYZ' + XYZ
endmodule

module ODD3 (
  input  X,
  input  Y,
  input  Z,
  output OUT
);

  wire and_1_out, and_2_out, and_3_out, and_4_out;

  and and_1 (and_1_out, ~X, ~Y, Z);  // AND_Gate
  and and_2 (and_2_out, ~X, Y, ~Z);  // AND_Gate
  and and_3 (and_3_out, X, ~Y, ~Z);  // AND_Gate
  and and_4 (and_4_out, X, Y, Z);
  or or_1 (OUT, and_1_out, and_2_out, and_3_out, and_4_out);

  // Notes on the sheet:
  //   ODD3: OUT = X'Y'Z + X'YZ' + XY'Z' + XYZ
endmodule

module PERSONAL_F (
  input  X,
  input  Y,
  input  Z,
  output OUT
);

  wire and_1_out, and_2_out, and_3_out, and_4_out, and_5_out, and_6_out;

  and and_1 (and_1_out, ~X, ~Y, Z);  // AND_Gate
  and and_2 (and_2_out, ~X, Y, Z);  // AND_Gate
  and and_3 (and_3_out, X, ~Y, ~Z);  // AND_Gate
  and and_4 (and_4_out, X, ~Y, Z);  // AND_Gate
  and and_5 (and_5_out, X, Y, ~Z);  // AND_Gate
  and and_6 (and_6_out, X, Y, Z);
  or or_1 (OUT, and_1_out, and_2_out, and_3_out, and_4_out, and_5_out, and_6_out);

  // Notes on the sheet:
  //   PERSONAL_F (ERP 36863, B=95=01011111): OUT = X'Y'Z + X'YZ + XY'Z' + XY'Z + XYZ' + XYZ
endmodule

module HALF_ADDER (
  input  X,
  input  Y,
  output S,
  output C
);

  XOR_SOP xor_sop_1 (.X(X), .Y(Y), .Z(S));
  and and_1 (C, X, Y);

  // Notes on the sheet:
  //   HALF_ADDER: S = X xor Y (XOR_SOP), C = XY
endmodule

module FULL_ADDER_A (
  input  X,
  input  Y,
  input  CIN,
  output S,
  output COUT
);

  ODD3 odd3_1 (.Y(Y), .Z(CIN), .X(X), .OUT(S));
  MAJ3 maj3_1 (.Y(Y), .Z(CIN), .X(X), .OUT(COUT));

  // Notes on the sheet:
  //   FULL_ADDER_A: S = ODD3(X,Y,CIN), COUT = MAJ3(X,Y,CIN)
endmodule

module FULL_ADDER_B (
  input  X,
  input  Y,
  input  CIN,
  output S,
  output COUT
);

  wire half_adder_1_c, half_adder_1_s, half_adder_2_c;

  HALF_ADDER half_adder_1 (.X(X), .Y(Y), .S(half_adder_1_s), .C(half_adder_1_c));
  HALF_ADDER half_adder_2 (.X(half_adder_1_s), .Y(CIN), .S(S), .C(half_adder_2_c));
  or or_1 (COUT, half_adder_2_c, half_adder_1_c);

  // Notes on the sheet:
  //   two HALF_ADDERs + one OR
  //   FULL_ADDER_B: S = (X xor Y) xor CIN, COUT = XY + (X xor Y)CIN
endmodule

module TESTBENCH (
  input  X,
  input  Y,
  input  CIN,
  output NORREF,
  output NORT,
  output NORDIFF,
  output SA,
  output COA,
  output SB,
  output COB,
  output MISMATCH
);

  wire xor_1_out, xor_2_out;

  FULL_ADDER_A full_adder_a_1 (.CIN(CIN), .X(X), .Y(Y), .S(SA), .COUT(COA));
  FULL_ADDER_B full_adder_b_1 (.Y(Y), .CIN(CIN), .X(X), .COUT(COB), .S(SB));
  NOR_T nor_t_1 (.X(X), .Y(Y), .Z(NORT));
  xor xor_1 (xor_1_out, SA, SB);
  xor xor_2 (xor_2_out, COA, COB);
  nor nor_1 (NORREF, X, Y);
  xor xor_3 (NORDIFF, NORT, NORREF);
  or or_1 (MISMATCH, xor_1_out, xor_2_out);

  // Other names for the same wires on the sheet: tCOA = COA; tCOB = COB; tNR = NORREF; tNT = NORT; tSA = SA; tSB = SB;
  //   tX = X; tY = Y

  // Notes on the sheet:
  //   TESTBENCH: FULL_ADDER_A vs FULL_ADDER_B, and NOR_T vs built-in NOR
  //   NOR_T check on X, Y (NORDIFF = NORT xor NORREF)
  //   MISMATCH = (SA xor SB) + (COA xor COB)
endmodule
